# Fritzing sketch Transmitter (saved by Fritzing 0.9.6b)
breadboards: 1

parts:
  TRANSMITTER = Arduino Nano (Rev3.0)
  part = Piezo Speaker [part_number=PIEZO]
  R1 = Resistor [tolerance=±5% resistance=220 package="0603 [SMD]"]
  LED1 = LED - 5mm [color="Red (633nm)" package="5 mm [THT]"]
  LED2 = Super Flux LED blue [color=Blue]

nets:
  N1: TRANSMITTER.GND, part.pin1, R1.Pin_0, LED2.cathode
  N2: TRANSMITTER.D4, part.pin2, LED1.cathode, LED2.anode
  N3: R1.Pin_1, LED1.anode
